# Fritzing sketch bathroom (saved by Fritzing 0.9.2b)
breadboards: 1

parts:
  Part1 = Arduino Yun
  JP1 = Header 3 [package=molex-1x3_lock]
  MQ-4_Methane_sensor = Header 3 [package=molex-1x3_lock]
  R1 = Resistor [tolerance=±5% resistance=4.7k package=THT]
  PIR_Motion_Sensor_1 = Header 3 [package=molex-1x3_lock]
  PIR_Motion_Sensor_2 = Header 3 [package=molex-1x3_lock]

nets:
  N1: Part1.A0, MQ-4_Methane_sensor.3
  N2: Part1.D2/SDA, Part1.D2, PIR_Motion_Sensor_1.3
  N3: Part1.D3/SCL, Part1.D3_PWM, PIR_Motion_Sensor_2.3
  N4: Part1.5V, JP1.1, JP1.2, JP1.3, PIR_Motion_Sensor_1.1, PIR_Motion_Sensor_2.1
  N5: Part1.GND, MQ-4_Methane_sensor.2, R1.Pin_0, PIR_Motion_Sensor_1.2, PIR_Motion_Sensor_2.2
  N6: MQ-4_Methane_sensor.1, R1.Pin_1
