# Fritzing sketch button (saved by Fritzing 0.9.2b)

parts:
  Part1 = Arduino Yun
  S2 = Pushbutton [package="[THT]"]

nets:
  N1: Part1.GND, S2.Pin_3, S2.Pin_4
  N2: Part1.D2/SDA, Part1.D2, S2.Pin_1, S2.Pin_2
