# Fritzing sketch food (saved by Fritzing 0.9.2b)

parts:
  Part1 = Arduino Yun
  Switch_with_LED = ENCODER_RGB_CA [package=encoder_led_3]

nets:
  N1: Part1.D2, Switch_with_LED.SW
  N2: Part1.5V, Switch_with_LED.-G
  N3: Part1.GND, Switch_with_LED.-R

notes:
  - GND
  - VCC
  - DIGITAL INPUT (switch state)
