# Fritzing sketch methane (saved by Fritzing 0.9.2b)
breadboards: 1

parts:
  Part1 = Arduino Yun
  JP1 = Header 3 [package=molex-1x3_lock]
  MQ-4_Methane_sensor = Header 3 [package=molex-1x3_lock]
  R1 = Resistor [tolerance=±5% resistance=4.7k package=THT]

nets:
  N1: Part1.A0, MQ-4_Methane_sensor.3
  N2: Part1.5V, JP1.1, JP1.2, JP1.3
  N3: Part1.GND, MQ-4_Methane_sensor.2, R1.Pin_0
  N4: MQ-4_Methane_sensor.1, R1.Pin_1
