# Fritzing sketch motion (saved by Fritzing 0.9.2b)

parts:
  Part1 = Arduino Yun
  PIR_Motion_Sensor = Header 3 [package=molex-1x3_lock]

nets:
  N1: Part1.D2, PIR_Motion_Sensor.1
  N2: Part1.5V, PIR_Motion_Sensor.3
  N3: Part1.GND, PIR_Motion_Sensor.2
