# Fritzing sketch sound (saved by Fritzing 0.9.2b)

parts:
  Part1 = Arduino Yun
  GATE\n = Header 5 [package=1x05-1mm]
  Sound_Sensor = Breakout Board for Electret Microphone  # not connected

nets:
  N1: Part1.A0, GATE\n.5
  N2: Part1.A1, GATE\n.4
  N3: Part1.D2, GATE\n.3
  N4: Part1.5V, GATE\n.2
  N5: Part1.GND, GATE\n.1

notes:
  - GND
  - VCC
  - GATE
  - ENVELOPE
  - AUDIO
